# Fritzing sketch TouchLessMidi (saved by Fritzing 0.9.6b)
breadboards: 1

parts:
  Mod1 = Raspberry Pi 4B
  Grove1 = Grove OLED 128x96
  U1 = TCM8240MD [package=tcm8240md]  # not connected
  RE1 = Rotary Encoder [package=THT]  # not connected

nets:
  3V3: Mod1.3V3, Grove1.VCC
  N1: Mod1.GPIO2, Grove1.SDA
  N2: Mod1.GPIO3, Mod1.GPIO4, Grove1.SCL
  GND: Mod1.GND, Grove1.GND
